// Logisim project D_Flip_Flop.circ as structural Verilog: 5 circuits, main circuit main
module main (
  input  D,
  output S,
  output Q,
  output Q_prime,
  output R
);

  wire Clk_out, nand_1_out, nand_4_out;

  Clock Clk (.out(Clk_out));
  nand nand_1 (nand_1_out, nand_4_out, S);
  nand nand_2 (S, nand_1_out, Clk_out);
  nand nand_3 (R, S, Clk_out, nand_4_out);
  nand nand_4 (nand_4_out, R, D);
  nand nand_5 (Q, S, Q_prime);
  nand nand_6 (Q_prime, Q, R);
endmodule

module Oppgave_1 (
  input  CLEAR,
  input  D,
  output S,
  output Q,
  output Q_prime,
  output R
);

  wire Clk_out, nand_1_out, nand_4_out, nand_5_out, not_1_out;

  Clock Clk (.out(Clk_out));
  nand nand_1 (nand_1_out, nand_4_out, S);
  nand nand_2 (S, nand_1_out, Clk_out);
  nand nand_3 (R, S, Clk_out, nand_4_out);
  nand nand_4 (nand_4_out, R, D);
  not not_1 (not_1_out, CLEAR);
  nand nand_5 (nand_5_out, S, Q_prime);
  nand nand_6 (Q_prime, nand_5_out, R);
  and and_1 (Q, not_1_out, nand_5_out);
endmodule

module Oppgave_2 (
  input  SET,
  input  D,
  output S,
  output Q,
  output Q_prime,
  output R
);

  wire and_1_out, Clk_out, nand_1_out, nand_4_out, nand_5_out;

  Clock Clk (.out(Clk_out));
  nand nand_1 (nand_1_out, nand_4_out, S);
  nand nand_2 (S, nand_1_out, Clk_out);
  nand nand_3 (R, S, Clk_out, nand_4_out);
  nand nand_4 (nand_4_out, R, D);
  and and_1 (and_1_out, Clk_out, SET);
  nand nand_5 (nand_5_out, S, Q_prime);
  nand nand_6 (Q_prime, nand_5_out, R);
  or or_1 (Q, and_1_out, nand_5_out);
endmodule

module Oppgave_3 (
  input  CE,
  input  D,
  output S,
  output Q,
  output Q_prime,
  output R
);

  wire and_1_out, Clk_out, nand_1_out, nand_4_out;

  Clock Clk (.out(Clk_out));
  and and_1 (and_1_out, CE, Clk_out);
  nand nand_1 (nand_1_out, nand_4_out, S);
  nand nand_2 (S, nand_1_out, and_1_out);
  nand nand_3 (R, S, and_1_out, nand_4_out);
  nand nand_4 (nand_4_out, R, D);
  nand nand_5 (Q, S, Q_prime);
  nand nand_6 (Q_prime, Q, R);
endmodule

module Oppgave_4 (
  input  D,
  output S,
  output Q,
  output Q_prime,
  output R
);

  wire Clk_out, nand_1_out, nand_4_out;

  Clock Clk (.out(Clk_out));
  nand nand_1 (nand_1_out, nand_4_out, S);
  nand nand_2 (S, nand_1_out, Clk_out);
  nand nand_3 (R, S, Clk_out, nand_4_out);
  nand nand_4 (nand_4_out, R, D);
  nand nand_5 (Q, S, Q_prime);
  nand nand_6 (Q_prime, Q, R);
endmodule
