// Logisim project kodelaas_aleksava.circ as structural Verilog: 2 circuits, main circuit main
module main (
);

  wire _1_out, _2_out, _3_out, _4_out, _5_out, _6_out, _7_out, clock_1_out, d_ff_1_q, d_ff_2_q,
       kombinatorisk_logikk_1_d0, kombinatorisk_logikk_1_d1, kombinatorisk_logikk_1_out;
  wire [2:0] priority_encoder_1_out;

  Button _1 (.out(_1_out));
  Button _4 (.out(_4_out));
  Button _7 (.out(_7_out));
  Button _2 (.out(_2_out));
  Button _5 (.out(_5_out));
  Button _8 ();  // open: out
  Button _3 (.out(_3_out));
  Button _6 (.out(_6_out));
  Button _9 ();  // open: out
  Kombinatorisk_Logikk kombinatorisk_logikk_1 (
    .Q0(d_ff_1_q), .Q1(d_ff_2_q), .X2(priority_encoder_1_out[2]), .X1(priority_encoder_1_out[1]),
    .X0(priority_encoder_1_out[0]), .D1(kombinatorisk_logikk_1_d1), .D0(kombinatorisk_logikk_1_d0),
    .Out(kombinatorisk_logikk_1_out));
  Priority_Encoder priority_encoder_1 (
    .in1(_1_out), .in2(_2_out), .in3(_3_out), .in4(_4_out), .in5(_5_out), .in6(_6_out), .in7(_7_out),
    .out(priority_encoder_1_out));  // open: in0, en_in, gs, en_out
  Clock clock_1 (.out(clock_1_out));
  D_Flip_Flop d_ff_1 (.clk(clock_1_out), .D(kombinatorisk_logikk_1_d1), .Q(d_ff_1_q));  // open: Qn, preset, en, reset
  D_Flip_Flop d_ff_2 (.clk(clock_1_out), .D(kombinatorisk_logikk_1_d0), .Q(d_ff_2_q));  // open: Qn, preset, en, reset
  LED Out (.in(kombinatorisk_logikk_1_out));

  // Notes on the sheet:
  //   Koden er:    1 2 4 
endmodule

module Kombinatorisk_Logikk (
  input  Q0,
  input  Q1,
  input  X2,
  input  X1,
  input  X0,
  output D1,
  output D0,
  output Out
);

  wire and_2_out, and_3_out, and_4_out, and_5_out, and_6_out, and_7_out, not_1_out, not_2_out, not_3_out,
       not_4_out, not_5_out, not_6_out, not_7_out, not_8_out, not_9_out, not_10_out, not_11_out, not_12_out,
       not_13_out, not_14_out, not_15_out, not_16_out, not_17_out, not_18_out;

  not not_1 (not_1_out, Q0);
  not not_2 (not_2_out, X2);
  not not_3 (not_3_out, X0);
  not not_4 (not_4_out, Q1);
  not not_5 (not_5_out, X2);
  not not_6 (not_6_out, X0);
  not not_7 (not_7_out, Q1);
  not not_8 (not_8_out, X1);
  not not_9 (not_9_out, X0);
  not not_10 (not_10_out, Q0);
  not not_11 (not_11_out, X2);
  not not_12 (not_12_out, X1);
  not not_13 (not_13_out, Q0);
  not not_14 (not_14_out, X2);
  not not_15 (not_15_out, X1);
  not not_16 (not_16_out, Q1);
  not not_17 (not_17_out, X1);
  not not_18 (not_18_out, X0);
  and and_1 (Out, Q0, Q1);
  and and_2 (and_2_out, not_1_out, Q1, not_2_out, X1, not_3_out);
  and and_3 (and_3_out, Q0, not_4_out, not_5_out, not_6_out);
  and and_4 (and_4_out, Q0, not_7_out, not_8_out, not_9_out);
  and and_5 (and_5_out, not_10_out, not_11_out, not_12_out, X0);
  and and_6 (and_6_out, not_13_out, Q1, not_14_out, not_15_out);
  and and_7 (and_7_out, Q0, not_16_out, X2, not_17_out, not_18_out);
  or or_1 (D1, and_2_out, and_3_out, and_4_out);
  or or_2 (D0, and_5_out, and_6_out, and_7_out);
endmodule
